# Fritzing sketch Radiodan_app (saved by Fritzing 0.8.3b)
breadboards: 1

parts:
  RaspberryPi1 = Raspberry Pi Model B
  R1 = Rotary Potentiometer (Small)
  S2 = Round Pushbutton
  S3 = Round Pushbutton
  S4 = Round Pushbutton
  S5 = Pushbutton [package="[THT]"]

nets:
  N1: RaspberryPi1.GND, RaspberryPi1.#4, S5.Pin_1, S5.Pin_2
  N2: RaspberryPi1.#17, S4.leg0
  N3: RaspberryPi1.#22, S3.leg1
  N4: RaspberryPi1.#23, R1.leg1
  N5: RaspberryPi1.#24, R1.leg2
  N6: RaspberryPi1.#25, S2.leg1

notes:
  next station
  previous station
  anticlockwise->lower volume
  clockwise->higher volume
  avoid
  on / off

custom parts:
  Raspberry Pi Model B: Raspberry Pi (Model B)
